# Fritzing sketch Clock_trinketPro (saved by Fritzing 0.9.2b)
breadboards: 1

parts:
  Part2 = Adafruit DS1307 RTC Breakout [part_number="Adafruit #264"]
  IC1 = MSGEQ7 [package=soic8]
  J1 = screw terminal, 6 pins
  JACK1 = 2.1mm DC Barrel Jack
  S1 = Toggle Switch [package=THT]
  R1 = Rotary Potentiometer (Small) [maximum_resistance=100kΩ package=THT]
  R2 = Rotary Potentiometer (Small) [maximum_resistance=100kΩ package=THT]
  R3 = Rotary Potentiometer (Small) [maximum_resistance=100kΩ package=THT]
  Part3 = Adafruit MAX9814 Electret Microphone Amplifier [part_number="Adafruit #1713"]
  Part4 = Adafruit Pro Trinket 5V 16MHz [part_number="Adafruit #2000"]
  R4 = Resistor [tolerance=±5% resistance=22k package="0805 [SMD]"]
  C1 = Ceramic Capacitor [capacitance="100 nF" package="0603 [SMD, multilayer]"]
  C2 = Ceramic Capacitor [capacitance="100 nF" package="0603 [SMD, multilayer]"]
  C3 = Ceramic Capacitor [capacitance="100 nF" package="0603 [SMD, multilayer]"]
  R5 = Resistor [tolerance=±5% resistance=200k package="0805 [SMD]"]
  C4 = Ceramic Capacitor [capacitance=0.1µF package="0603 [SMD, multilayer]"]
  R6 = Resistor [tolerance=±5% resistance=330 package=THT]
  R8 = Resistor [tolerance=±5% resistance=330 package=THT]
  J2 = Screw terminal - 2 pins [package=THT]
  J3 = screw terminal, 3 pins
  C5 = Capacitor Polarized [package=nippon_f80]
  R9 = Resistor [tolerance=±5% resistance=470 package="0805 [SMD]"]

nets:
  N1: Part2.SQW, IC1.DCOUT, Part4.A3
  N2: Part2.SCL, Part4.A4
  N3: Part2.SDA, Part4.A5
  VDD: Part2.VCC, IC1.VDD, J1.pin2, JACK1.center, R1.leg1, R2.leg1, R3.leg1, Part3.VDD, Part4.VBAT, R4.Pin_1, R5.Pin_1, C4.1, R8.Pin_0, J2.pin1, J3.pin3, C5.+
  GND: Part2.GND, IC1.GND, J1.pin1, JACK1.sleeve, R1.leg2, R2.leg2, R3.leg2, Part3.GND, Part4.GND, C2.0, C3.0, C4.0, R6.Pin_0, J2.pin2, J3.pin1, C5.-
  N4: IC1.STROBE, Part4.D8
  N5: IC1.AUDIO_IN, C1.0
  N6: IC1.CG, C2.1
  N7: IC1.RESET, Part4.D10
  N8: IC1.CKIN, C3.1, R5.Pin_0
  N9: J1.pin3, Part3.OUTPUT
  N10: J1.pin4, R3.wiper, Part4.A0
  N11: J1.pin5, R2.wiper, Part4.A1
  N12: J1.pin6, R1.wiper, Part4.D9, Part4.A2
  N13: S1.L1, R8.Pin_1
  N14: S1.COM, Part4.D6
  N15: S1.L2, R6.Pin_1
  N16: Part4.D3, R9.Pin_0
  N17: R4.Pin_0, C1.1
  N18: J3.pin2, R9.Pin_1

custom parts:
  Adafruit DS1307 RTC Breakout: This is a great battery-backed real time clock (RTC) that allows your microcontroller project to keep track of time even if it is reprogrammed, or if the power is lost. Perfect for datalogging, clock-building, time stamping, timers and alarms, etc. The DS1307 is the most popular RTC - but it requires 5V power to work (although we've used it with 5V power and 3.3V logic successfully) PCB &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
  2.1mm DC Barrel Jack: 2.1mm DC Barrel Jack with Thru-Hole Connectors (breadboardable)
  Adafruit MAX9814 Electret Microphone Amplifier: Add an ear to your project with this well-designed electret microphone amplifier with AGC. This fully assembled and tested board comes with a 20-20KHz electret microphone soldered on. For the amplification, we use the Maxim MAX9814, a specialty chip that is designed for amplifying electret microphones in situations where the loudness of the audio isn't predictable. This fancy microphone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
  Adafruit Pro Trinket 5V 16MHz: Trinket's got a big sister in town - the Pro Trinket 5V! Pro Trinket combines everything you love about Trinket with the familiarity of the common core Arduino chip, the ATmega328. It's like an Arduino Pro Mini with more pins and USB tossed in, so delicious. Trinket's a year old now, and while its been great to see tons of tiny projects, sometimes you just need more pins, more FLASH, and more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
